# Fritzing sketch Waist Wiring2 (saved by Fritzing 0.9.3b)

parts:
  Part1 = Adafruit TCA9548A
  Part2 = Adafruit LM3671 Buck Converter [part_number="Adafruit #2745"]
  U2 = RJ45 Jack [package=rj45-8]
  U3 = RJ45 Jack [package=rj45-8]
  U4 = RJ45 Jack [package=rj45-8]

nets:
  N1: Part1.2SDA, U4.7
  N2: Part1.2SCL, U4.8
  N3: Part1.3SDA, U3.4
  N4: Part1.3SCL, U3.3
  N5: Part1.4SDA, U3.7
  N6: Part1.4SCL, U3.8
  VCC: Part1.VCC, Part1.A0, Part2.3.3V, U3.1, U4.1
  GND: Part1.GND, Part2.GND, U2.5, U3.2, U4.2
  N7: Part1.INPUTSDA, U2.3
  N8: Part1.INPUTSCL, U2.4
  N9: Part1.1SDA, U4.4
  N10: Part1.1SCL, U4.3
  N11: Part2.VIN, U2.6

custom parts:
  Adafruit TCA9548A: You just found the perfect I2C sensor, and you want to wire up two or three or more of them to your Arduino when you realize "Uh oh, this chip has a fixed I2C address, and from what I know about I2C, you cannot have two devices with the same address on the same SDA/SCL pins!" Are you out of luck? You would be, if you didn't have this ultra-cool TCA9548A 1-to-8 I2C multiplexer! Finally, a way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
  Adafruit LM3671 Buck Converter: Your power supply problems just got SUPER SOLVED! This 3.3V Buck Converter Breakout board is great for supplying power to low voltage circuits from a single Li-Ion cell battery or USB power. This chip provides up to 600-mA load current across the entire input voltage range of 3.5 to 5.5V. Great for your portable project, we made this "pin compatible" with the LM1117-3.3V TO-220 chip so you can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
  RJ45 Jack: RJ45 Jack Simple RJ45, 8-pin connection - connector for common Cat5, Cat5e, and Cat6 Ethernet cables. Footprint not yet proven in production. Connector sku is PRT-00643; Breakout PCB sku is BOB-00716.
